# Fritzing sketch braco_bluetooth_esquema (saved by Fritzing 0.9.5d)

parts:
  Componente1 = Arduino Uno (Rev3) - ICSP
  Componente2 = Bluetooth HC-05 Macho
  J1 = Basic Servo
  J2 = Basic Servo
  J3 = Basic Servo
  J4 = Basic Servo
  VCC1 = Battery
  BAT1 = BC9VPC [package=bc9vpc]

nets:
  N1: Componente1.ICSP_MOSI, Componente1.D11_PWM/MOSI, Componente2.TXD
  N2: Componente1.D9_PWM, J3.pulse
  N3: Componente1.D10_PWM/SS, Componente2.RXD
  GND: Componente1.GND, Componente2.GND, J1.gnd, VCC1.-
  N4: Componente1.D3_PWM, J1.pulse
  N5: Componente1.D5_PWM, J2.pulse
  N6: Componente1.D6_PWM, J4.pulse
  N7: Componente1.3V3, VCC1.+
  N8: J2.gnd, BAT1.V-
  N9: J2.vcc, BAT1.V+

notes:
  Base (A)
  Ombro (B)
  Cotovelo (C)
  Garra (D)
